# Fritzing sketch unity-controller-firmware (saved by Fritzing 0.9.3b)
breadboards: 1

parts:
  VCC1 = 4 x AAA Battery Mount [part_number=https://www.adafruit.com/product/830]
  Part1 = Photon
  Part2 = Adafruit MMA8451 Accelerometer [part_number=https://www.adafruit.com/product/2019]
  Part3 = Adafruit DRV2605L [part_number=https://www.adafruit.com/product/2305]
  MOTOR1 = Vibration Motor [part_number=https://www.adafruit.com/product/1201]
  U1 = TMP36 [part_number=https://www.adafruit.com/product/165 package=to-92]
  R1 = Photocell (LDR) [part_number=https://www.adafruit.com/product/161 package=THT]
  R2 = Resistor [tolerance=±5% resistance=10k package=THT]
  J1 = Piezo Speaker [part_number=https://www.adafruit.com/product/160]
  LED2 = RGB LED (com. cathode, rbg) [part_number=https://www.adafruit.com/product/1938 package="5 mm [THT]"]
  PIR1 = PIR sensor

nets:
  GND: VCC1.-, Part1.GND, Part2.GND, Part3.GND, U1.GND, R2.Pin_1, J1.pin2, LED2.GND, PIR1.GND
  VIN: VCC1.+, Part1.VIN, PIR1.VDD
  N1: Part1.A0, U1.VOUT
  N2: Part1.A1, R1.pin_0, R2.Pin_0
  N3: Part1.D0, Part2.SDA, Part3.SDA
  N4: Part1.D1, Part2.SCL, Part3.SCL
  N5: Part1.D2, PIR1.SIG
  N6: Part1.D3, J1.pin1
  N7: Part1.D6, LED2.DATA_IN
  3V3: Part1.3V3, Part2.+3V3, Part3.VIN, U1.VCC, R1.pin_1, LED2.+5
  N8: Part3.OUT+, MOTOR1.NEG
  N9: Part3.OUT-, MOTOR1.POS

notes:
  +3.3V
  GND
  5mm NEOPIXEL<module fritzingVersion="0.9.3b.04.19.5c895d327c44a3114e5fcc9d8260daf0cbb52806">
  <boundingRects>
  <boundingRect name="PCB View" rect="0 0 0 0"/>
  <boundingRect name="Breadboard View" rect="372.381 188.582 122.802 77"/>
  <boundingRect name="Schematic View" rect="0 0 0 0"/>
  </boundingRects>
  <instances>
  <instance moduleIdRef="NoteModuleID" path=":/resources/parts/core/note.fzp" modelIndex="85439408">
  <title>Note1</title>
  <text>&lt;!DOCTYPE HTML PUBLIC "-//W3C//DTD HTML 4.0//EN" "http://www.w3.org/TR/REC-html40/strict.dtd">
  &lt;html>&lt;head>&lt;meta name="qrichtext" content="1" />&lt;style type="text/css">
  p, li { white-space: pre-wrap; }
  &lt;/style>&lt;/head>&lt;body style=" font-family:'Droid Sans'; font-size:9pt; font-weight:400; font-style:normal;">
  &lt;p style=" margin-top:0px; margin-bottom:0px; margin-left:0px; margin-right:0px; -qt-block-indent:0; text-indent:0px;">5mm Neopixel Pinout&lt;/p>
  &lt;p style=" margin-top:0px; margin-bottom:0px; margin-left:0px; margin-right:0px; -qt-block-indent:0; text-indent:0px;">1: Data IN [LEFT] (short)&lt;/p>
  &lt;p style=" margin-top:0px; margin-bottom:0px; margin-left:0px; margin-right:0px; -qt-block-indent:0; text-indent:0px;">2: +V (short)&lt;/p>
  &lt;p style=" margin-top:0px; margin-bottom:0px; margin-left:0px; margin-right:0px; -qt-block-indent:0; text-indent:0px;">3: GND (long)&lt;/p>
  &lt;p style=" margin-top:0px; margin-bottom:0px; margin-left:0px; margin-right:0px; -qt-block-indent:0; text-indent:0px;">4: Data OUT [RIGHT] (long)&lt;/p>&lt;/body>&lt;/html></text>
  <views>
  <breadboardView layer="breadboardNote">
  <geometry x="372.381" y="188.582" z="6.5" width="122.802" height="77"/>
  </breadboardView>
  </views>
  </instance>
  </instances>
  </module>
  1: Data IN [LEFT] (short)
  2: +V (short)
  3: GND (long)
  4: Data OUT [RIGHT] (long)
  +6V
  PIEZO BUZZER
  D3
  TEMPERATURE SENSOR
  LEFT -> 3V3
  MIDDLE -> A0
  RIGHT -> GND
  PHOTOCELL
  A1
  PIR SENSOR
  needs more than 3v3 to operate
  BLACK -> GND
  RED -> VIN (4.7-6VDC)
  YELLOW -> D2
  VIBE MOTOR
  No polarity
  HAPTIC DRIVER
  SDA -> D0
  SCL -> D1
  GND -> GND
  VIN -> 3V3
  ACCELEROMETER
  SDA -> D0
  SCL -> D1
  GND -> GND
  VIN -> 3V3
  BATTERY HOLDER
  RED -> VIN
  BLACK -> GND

custom parts:
  Adafruit MMA8451 Accelerometer: So many accelerometers and so little time! We've expanded our accelerometer selection even more with this high-precision and inexpensive MMA8451 Triple-Axis Accelerometer w/ 14-bit ADC. You can detect motion, tilt and basic orientation with a digital accelerometer - and the MMA8451 is a great accelerometer to start with. It has a wide usage range, from +-2g up to +-8g yet is easy to use with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
  Adafruit DRV2605L: The DRV2605 from TI is a fancy little motor driver. Rather than controlling a stepper motor or DC motor, its designed specifically for controlling haptic motors - buzzers and vibration motors. Normally one would just turn those kinds of motors on and off, but this driver has the ability to have various effects when driving a vibe motor. For example, ramping the vibration level up and down,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
  Vibration Motor: An eccentric vibration motor!
  RGB LED (com. cathode, rbg): A 5mm tri-color LED with red, green and blue inside. Pin order: red - com. cathode - blue - green
